// Logisim project jrmips.circ as structural Verilog: 6 circuits, main circuit MAIN
module Field (
  input  [15:0] Instruction,
  output Subop,
  output [2:0] Rt,
  output [2:0] Rs,
  output [3:0] Opcode
);


  assign Opcode = Instruction[15:12];
  assign Rs = Instruction[11:9];
  assign Rt = Instruction[8:6];
  assign Subop = Instruction[0];
endmodule

// RegFile
module RegisterFile (
  input  [2:0] Rt,
  input  [2:0] Rs,
  input  [15:0] Data1,
  input  [2:0] WriteReg0,
  input  [15:0] Data2,
  input  Clock,
  input  [2:0] WriteReg1,
  input  WriteEnable,
  output [15:0] ReadDataT,
  output [15:0] ReadDataS
);

  wire demultiplexer_3_out0, demultiplexer_3_out1, demultiplexer_3_out2, demultiplexer_3_out3,
       demultiplexer_3_out4, demultiplexer_3_out5, demultiplexer_3_out6, demultiplexer_3_out7;
  wire [2:0] adder_1_out;
  wire [15:0] demultiplexer_1_out0, demultiplexer_1_out1, demultiplexer_1_out2, demultiplexer_1_out3,
       demultiplexer_1_out4, demultiplexer_1_out5, demultiplexer_1_out6, demultiplexer_1_out7,
       demultiplexer_2_out0, demultiplexer_2_out1, demultiplexer_2_out2, demultiplexer_2_out3,
       demultiplexer_2_out4, demultiplexer_2_out5, demultiplexer_2_out6, demultiplexer_2_out7, or_1_out,
       or_2_out, or_3_out, or_4_out, or_5_out, or_6_out, or_7_out, or_8_out, r0_q, r1_q, r2_q, r3_q, r4_q,
       r5_q, r6_q, r7_q;

  Demultiplexer #(.select(3), .width(16)) demultiplexer_1 (
    .out0(demultiplexer_1_out0), .out1(demultiplexer_1_out1), .out2(demultiplexer_1_out2),
    .out3(demultiplexer_1_out3), .out4(demultiplexer_1_out4), .out5(demultiplexer_1_out5),
    .out6(demultiplexer_1_out6), .out7(demultiplexer_1_out7), .in(Data1), .sel(WriteReg0), .en(WriteEnable));
  Demultiplexer #(.select(3), .width(16)) demultiplexer_2 (
    .out0(demultiplexer_2_out0), .out1(demultiplexer_2_out1), .out2(demultiplexer_2_out2),
    .out3(demultiplexer_2_out3), .out4(demultiplexer_2_out4), .out5(demultiplexer_2_out5),
    .out6(demultiplexer_2_out6), .out7(demultiplexer_2_out7), .in(Data2), .sel(adder_1_out), .en(WriteEnable));
  Adder #(.width(3)) adder_1 (.a(WriteReg1), .b(3'b001), .out(adder_1_out));  // open: cin, cout
  Demultiplexer #(.select(3)) demultiplexer_3 (
    .out0(demultiplexer_3_out0), .out1(demultiplexer_3_out1), .out2(demultiplexer_3_out2),
    .out3(demultiplexer_3_out3), .out4(demultiplexer_3_out4), .out5(demultiplexer_3_out5),
    .out6(demultiplexer_3_out6), .out7(demultiplexer_3_out7), .in(WriteEnable), .sel(WriteReg0));  // open: en
  assign or_1_out = demultiplexer_1_out0 | demultiplexer_2_out0;  // OR_Gate or_1, 16 bits wide
  assign or_2_out = demultiplexer_1_out1 | demultiplexer_2_out1;  // OR_Gate or_2, 16 bits wide
  assign or_3_out = demultiplexer_1_out2 | demultiplexer_2_out2;  // OR_Gate or_3, 16 bits wide
  assign or_4_out = demultiplexer_1_out3 | demultiplexer_2_out3;  // OR_Gate or_4, 16 bits wide
  assign or_5_out = demultiplexer_1_out4 | demultiplexer_2_out4;  // OR_Gate or_5, 16 bits wide
  assign or_6_out = demultiplexer_1_out5 | demultiplexer_2_out5;  // OR_Gate or_6, 16 bits wide
  assign or_7_out = demultiplexer_1_out6 | demultiplexer_2_out6;  // OR_Gate or_7, 16 bits wide
  assign or_8_out = demultiplexer_1_out7 | demultiplexer_2_out7;  // OR_Gate or_8, 16 bits wide
  Register #(.width(16)) r0 (.D(or_1_out), .en(demultiplexer_3_out0), .Q(r0_q), .clk(Clock));  // open: clr
  Register #(.width(16)) r1 (.D(or_2_out), .en(demultiplexer_3_out1), .Q(r1_q), .clk(Clock));  // open: clr
  Register #(.width(16)) r2 (.D(or_3_out), .en(demultiplexer_3_out2), .Q(r2_q), .clk(Clock));  // open: clr
  Register #(.width(16)) r3 (.D(or_4_out), .en(demultiplexer_3_out3), .Q(r3_q), .clk(Clock));  // open: clr
  Register #(.width(16)) r4 (.D(or_5_out), .en(demultiplexer_3_out4), .Q(r4_q), .clk(Clock));  // open: clr
  Register #(.width(16)) r5 (.D(or_6_out), .en(demultiplexer_3_out5), .Q(r5_q), .clk(Clock));  // open: clr
  Register #(.width(16)) r6 (.D(or_7_out), .en(demultiplexer_3_out6), .Q(r6_q), .clk(Clock));  // open: clr
  Register #(.width(16)) r7 (.D(or_8_out), .en(demultiplexer_3_out7), .Q(r7_q), .clk(Clock));  // open: clr
  Multiplexer #(.select(3), .width(16), .enable("false")) multiplexer_1 (
    .in0(r0_q), .in1(r1_q), .in2(r2_q), .in3(r3_q), .in4(r4_q), .in5(r5_q), .in6(r6_q), .in7(r7_q),
    .out(ReadDataT), .sel(Rt));
  Multiplexer #(.select(3), .width(16), .enable("false")) multiplexer_2 (
    .in0(r0_q), .in1(r1_q), .in2(r2_q), .in3(r3_q), .in4(r4_q), .in5(r5_q), .in6(r6_q), .in7(r7_q),
    .out(ReadDataS), .sel(Rs));
endmodule

module ALU (
  input  [15:0] ReadDataT,
  input  [15:0] ReadDataS,
  input  [2:0] Oper,
  output Zero,
  output [15:0] ALUout,
  output Larger,
  output Smaller,
  output [15:0] Upper,
  output [15:0] Rem
);

  wire comparator_1_eq;
  wire [15:0] adder_1_out, and_1_out, divider_1_out, multiplier_1_out, nor_1_out, shifter_1_out,
       shifter_2_out, subtractor_1_out;

  Adder #(.width(16)) adder_1 (.a(ReadDataT), .b(ReadDataS), .out(adder_1_out));  // open: cin, cout
  Subtractor #(.width(16)) subtractor_1 (.a(ReadDataT), .b(ReadDataS), .out(subtractor_1_out));  // open: bin, bout
  assign nor_1_out = ~(ReadDataT | ReadDataS);  // NOR_Gate nor_1, 16 bits wide
  assign and_1_out = ReadDataT & ReadDataS;  // AND_Gate and_1, 16 bits wide
  Multiplier #(.width(16)) multiplier_1 (
    .a(ReadDataT), .b(ReadDataS), .out(multiplier_1_out), .cout(Upper));  // open: cin
  Divider #(.width(16)) divider_1 (.a(ReadDataT), .b(ReadDataS), .out(divider_1_out), .rem(Rem));  // open: upper
  Shifter #(.width(16)) shifter_1 (.in(ReadDataS), .\dist (ReadDataT[3:0]), .out(shifter_1_out));
  Shifter #(.width(16), .shift("lr")) shifter_2 (.in(ReadDataS), .\dist (ReadDataT[3:0]), .out(shifter_2_out));
  Comparator #(.width(16)) comparator_1 (
    .a(ReadDataS), .b({16{1'b0}}), .gt(Larger), .eq(comparator_1_eq), .lt(Smaller));
  Comparator #(.width(16)) comparator_2 (.a({16{1'b0}}), .b(subtractor_1_out), .eq(Zero));  // open: gt, lt
  Multiplexer #(.select(3), .width(16), .enable("false")) multiplexer_1 (
    .in0(adder_1_out), .in1(subtractor_1_out), .in2(nor_1_out), .in3(and_1_out), .in4(multiplier_1_out),
    .in5(divider_1_out), .in6(shifter_1_out), .in7(shifter_2_out), .out(ALUout), .sel(Oper));
endmodule

module DECODER2 (
  input  OPCODE3,
  input  OPCODE2,
  input  OPCODE1,
  input  OPCODE0,
  input  SUBOP,
  output Str,
  output Ld,
  output DataMemory,
  output HEXMux,
  output HALT
);

  wire and_3_out, and_4_out, and_5_out, not_1_out, not_2_out, not_3_out, not_5_out, not_6_out, not_7_out,
       not_8_out, not_9_out, not_10_out;

  not not_1 (not_1_out, OPCODE3);
  not not_2 (not_2_out, OPCODE3);
  not not_3 (not_3_out, SUBOP);
  not not_4 (DataMemory, OPCODE3);
  not not_5 (not_5_out, OPCODE3);
  not not_6 (not_6_out, OPCODE2);
  not not_7 (not_7_out, OPCODE2);
  not not_8 (not_8_out, OPCODE2);
  and and_1 (Str, not_1_out, OPCODE2, OPCODE1, OPCODE0, SUBOP);
  and and_2 (Ld, not_2_out, OPCODE2, OPCODE1, OPCODE0, not_3_out);
  and and_3 (and_3_out, not_5_out, not_6_out);
  not not_9 (not_9_out, OPCODE1);
  not not_10 (not_10_out, OPCODE0);
  and and_4 (and_4_out, not_7_out, SUBOP);
  and and_5 (and_5_out, OPCODE3, OPCODE2);
  and and_6 (HALT, OPCODE3, not_8_out, OPCODE1, OPCODE0, SUBOP);
  or or_1 (HEXMux, and_3_out, not_9_out, not_10_out, and_4_out, and_5_out);
endmodule

module DECODER1 (
  input  OPCODE3,
  input  OPCODE2,
  input  OPCODE1,
  input  OPCODE0,
  input  SUBOP,
  input  Zero,
  input  Larger,
  input  Smaller,
  input  HALT,
  output Oper2,
  output Oper1,
  output Oper0,
  output WriteEn,
  output DIM1,
  output DIM0,
  output ARS,
  output addi,
  output UII,
  output DivMul,
  output PCMux1,
  output PCMux0
);

  wire and_1_out, and_2_out, and_3_out, and_5_out, and_6_out, and_8_out, and_9_out, and_10_out, and_11_out,
       and_12_out, and_13_out, and_14_out, and_15_out, and_16_out, and_17_out, and_18_out, and_21_out,
       and_22_out, and_23_out, and_24_out, and_25_out, and_26_out, and_27_out, and_28_out, and_29_out,
       not_1_out, not_2_out, not_3_out, not_4_out, not_5_out, not_6_out, not_7_out, not_8_out, not_9_out,
       not_10_out, not_11_out, not_12_out, not_13_out, not_14_out, not_15_out, not_16_out, not_17_out,
       not_18_out, not_19_out, not_20_out, not_21_out, not_22_out, not_23_out, not_24_out, not_25_out,
       not_26_out, not_27_out, not_28_out, not_29_out, not_30_out, not_31_out, not_32_out, not_33_out,
       not_34_out, not_35_out, not_36_out, not_37_out, not_38_out, not_39_out, not_40_out, not_41_out;

  not not_1 (not_1_out, OPCODE1);
  not not_2 (not_2_out, OPCODE0);
  not not_3 (not_3_out, OPCODE1);
  not not_4 (not_4_out, OPCODE0);
  not not_5 (not_5_out, OPCODE2);
  not not_6 (not_6_out, OPCODE1);
  not not_7 (not_7_out, OPCODE0);
  not not_8 (not_8_out, SUBOP);
  not not_9 (not_9_out, OPCODE0);
  not not_10 (not_10_out, SUBOP);
  not not_11 (not_11_out, OPCODE3);
  not not_12 (not_12_out, OPCODE2);
  not not_13 (not_13_out, OPCODE3);
  not not_14 (not_14_out, OPCODE1);
  not not_15 (not_15_out, OPCODE0);
  not not_16 (not_16_out, OPCODE2);
  not not_17 (not_17_out, OPCODE1);
  not not_18 (not_18_out, OPCODE0);
  not not_19 (not_19_out, OPCODE2);
  not not_20 (not_20_out, OPCODE1);
  not not_21 (not_21_out, SUBOP);
  not not_22 (not_22_out, SUBOP);
  and and_1 (and_1_out, OPCODE2, OPCODE1, OPCODE0);
  and and_2 (and_2_out, OPCODE3, OPCODE0);
  and and_3 (and_3_out, OPCODE3, OPCODE1);
  and and_4 (ARS, OPCODE2, OPCODE1, OPCODE0, SUBOP);
  not not_23 (not_23_out, OPCODE3);
  not not_24 (not_24_out, OPCODE2);
  not not_25 (not_25_out, OPCODE1);
  not not_26 (not_26_out, OPCODE2);
  not not_27 (not_27_out, SUBOP);
  not not_28 (not_28_out, OPCODE0);
  not not_29 (not_29_out, OPCODE1);
  not not_30 (not_30_out, Smaller);
  not not_31 (not_31_out, HALT);
  not not_32 (not_32_out, OPCODE1);
  not not_33 (not_33_out, SUBOP);
  not not_34 (not_34_out, Zero);
  not not_35 (not_35_out, OPCODE1);
  not not_36 (not_36_out, OPCODE0);
  not not_37 (not_37_out, SUBOP);
  not not_38 (not_38_out, OPCODE0);
  not not_39 (not_39_out, OPCODE1);
  not not_40 (not_40_out, SUBOP);
  not not_41 (not_41_out, OPCODE0);
  and and_5 (and_5_out, OPCODE1, OPCODE0);
  and and_6 (and_6_out, OPCODE2, not_1_out, not_2_out);
  and and_7 (Oper1, not_3_out, not_4_out);
  and and_8 (and_8_out, not_5_out, not_6_out, not_7_out, not_8_out);
  and and_9 (and_9_out, OPCODE1, not_9_out, SUBOP);
  and and_10 (and_10_out, OPCODE1, OPCODE0, not_10_out);
  and and_11 (and_11_out, OPCODE2, SUBOP);
  and and_12 (and_12_out, OPCODE2, OPCODE0);
  and and_13 (and_13_out, OPCODE2, OPCODE1);
  and and_14 (and_14_out, not_11_out, not_12_out);
  and and_15 (and_15_out, not_13_out, not_14_out, not_15_out);
  and and_16 (and_16_out, not_16_out, not_17_out, not_18_out);
  and and_17 (and_17_out, not_19_out, not_20_out, not_21_out);
  and and_18 (and_18_out, OPCODE2, OPCODE1, OPCODE0, not_22_out);
  or or_1 (DIM0, and_1_out, and_2_out, and_3_out);
  and and_19 (addi, not_23_out, not_24_out, not_25_out, OPCODE0);
  and and_20 (UII, not_26_out, not_27_out);
  or or_2 (DivMul, not_28_out, SUBOP);
  and and_21 (and_21_out, OPCODE3, not_29_out, OPCODE0, Zero, Larger, not_30_out, not_31_out);
  and and_22 (and_22_out, OPCODE3, OPCODE0, SUBOP);
  and and_23 (and_23_out, OPCODE2, not_32_out, OPCODE0, not_33_out, not_34_out);
  and and_24 (and_24_out, OPCODE2, not_35_out, OPCODE0, SUBOP, Zero);
  and and_25 (and_25_out, OPCODE2, OPCODE1, not_36_out, not_37_out, Larger);
  and and_26 (and_26_out, OPCODE2, OPCODE1, not_38_out, SUBOP, Smaller);
  and and_27 (and_27_out, OPCODE3, not_39_out, OPCODE0, not_40_out);
  and and_28 (and_28_out, OPCODE3, OPCODE1, not_41_out);
  and and_29 (and_29_out, OPCODE3, OPCODE1, SUBOP);
  or or_3 (Oper2, and_5_out, and_6_out);
  or or_4 (Oper0, and_8_out, and_9_out, and_10_out, and_11_out, and_12_out, and_13_out);
  or or_5 (WriteEn, and_14_out, and_15_out, and_16_out, and_17_out, and_18_out);
  or or_6 (PCMux1, and_21_out, and_22_out);
  or or_7 (PCMux0, and_23_out, and_24_out, and_25_out, and_26_out, and_27_out, and_28_out, and_29_out);

  assign DIM1 = OPCODE3;
endmodule

module MAIN (
);

  wire addi, and_1_out, ARS, clock_1_out, DataMemory, DivMul, field_1_subop, HALT, HEXMux, L, Ld, not_1_out,
       not_2_out, S, Str, UII, WriteEn, Zero;
  wire [1:0] DIM, PCMux;
  wire [2:0] field_1_rs, field_1_rt, Oper;
  wire [3:0] bit_extender_2_out, bit_extender_2_out_2, bit_extender_2_out_3, bit_extender_2_out_4,
       field_1_opcode, register_1_q, register_1_q_2, register_1_q_3, register_1_q_4;
  wire [7:0] adder_1_out, multiplexer_6_out, PC_q;
  wire [15:0] alu_1_aluout, alu_1_rem, alu_1_upper, and_2_out, bit_extender_1_out, bit_extender_3_out,
       bit_extender_4_out, multiplexer_1_out, multiplexer_2_out, multiplexer_3_out, multiplexer_4_out,
       multiplexer_5_out, ram_1_data, registerfile_1_readdatas, registerfile_1_readdatat, rom_1_data;

  not not_1 (not_1_out, HALT);
  LED led_1 (.in(not_1_out));
  Register PC (.D(multiplexer_6_out), .en(and_1_out), .Q(PC_q), .clk(clock_1_out));  // open: clr
  and and_1 (and_1_out, 1'b1, not_1_out);
  Clock clock_1 (.out(clock_1_out));
  Hex_Digit_Display hex_digit_display_1 (.value(register_1_q_4));  // open: dp
  Hex_Digit_Display hex_digit_display_2 (.value(bit_extender_2_out_4));  // open: dp
  Hex_Digit_Display hex_digit_display_3 (.value(register_1_q_3));  // open: dp
  Hex_Digit_Display hex_digit_display_4 (.value(bit_extender_2_out_3));  // open: dp
  Adder adder_1 (.a(PC_q), .b(8'h1), .out(adder_1_out));  // open: cin, cout
  Hex_Digit_Display hex_digit_display_5 (.value(register_1_q_2));  // open: dp
  Hex_Digit_Display hex_digit_display_6 (.value(register_1_q));  // open: dp
  Hex_Digit_Display hex_digit_display_7 (.value(bit_extender_2_out_2));  // open: dp
  Hex_Digit_Display hex_digit_display_8 (.value(bit_extender_2_out));  // open: dp
  DECODER1 decoder1_1 (
    .OPCODE3(field_1_opcode[3]), .OPCODE2(field_1_opcode[2]), .OPCODE1(field_1_opcode[1]),
    .OPCODE0(field_1_opcode[0]), .SUBOP(field_1_subop), .Zero(Zero), .Larger(L), .Smaller(S),
    .Oper2(Oper[2]), .Oper1(Oper[1]), .Oper0(Oper[0]), .WriteEn(WriteEn), .DIM1(DIM[1]), .DIM0(DIM[0]),
    .ARS(ARS), .addi(addi), .UII(UII), .DivMul(DivMul), .PCMux1(PCMux[1]), .PCMux0(PCMux[0]));  // open: HALT
  Field field_1 (
    .Instruction(rom_1_data), .Subop(field_1_subop), .Rt(field_1_rt), .Rs(field_1_rs), .Opcode(field_1_opcode));
  ROM #(.dataWidth(16)) rom_1 (.addr(PC_q), .data(rom_1_data));  // open: sel
  Multiplexer #(.select(2), .width(16)) multiplexer_1 (
    .in0(alu_1_aluout), .in1(ram_1_data),
    .in2({bit_extender_2_out_4, bit_extender_2_out_3, bit_extender_2_out_2, bit_extender_2_out}),
    .in3(bit_extender_1_out), .out(multiplexer_1_out), .sel(DIM));  // open: en
  RegisterFile registerfile_1 (
    .Rt(field_1_rt), .Rs(field_1_rs), .Data1(multiplexer_1_out), .WriteReg0(field_1_rs),
    .Data2(multiplexer_2_out), .WriteReg1(field_1_rs), .WriteEnable(WriteEn),
    .ReadDataT(registerfile_1_readdatat), .ReadDataS(registerfile_1_readdatas), .Clock(clock_1_out));
  Register #(.width(16)) register_1 (
    .D(registerfile_1_readdatas), .en(not_2_out),
    .Q({register_1_q_4, register_1_q_3, register_1_q_2, register_1_q}), .clk(clock_1_out));  // open: clr
  not not_2 (not_2_out, HEXMux);
  DECODER2 decoder2_1 (
    .OPCODE3(field_1_opcode[3]), .OPCODE2(field_1_opcode[2]), .OPCODE1(field_1_opcode[1]),
    .OPCODE0(field_1_opcode[0]), .SUBOP(field_1_subop), .Str(Str), .Ld(Ld), .DataMemory(DataMemory),
    .HEXMux(HEXMux), .HALT(HALT));
  assign bit_extender_1_out = {{8{adder_1_out[7]}}, adder_1_out};  // Bit_Extender bit_extender_1
  Multiplexer #(.width(16)) multiplexer_2 (
    .in0(alu_1_rem), .in1(alu_1_upper), .out(multiplexer_2_out), .sel(DivMul));  // open: en
  assign {bit_extender_2_out_4, bit_extender_2_out_3, bit_extender_2_out_2, bit_extender_2_out} = {{8{1'b0}}, rom_1_data[8:1]};  // Bit_Extender bit_extender_2
  Multiplexer #(.width(16)) multiplexer_3 (
    .in0(registerfile_1_readdatat), .in1(multiplexer_4_out), .out(multiplexer_3_out), .sel(addi));  // open: en
  Multiplexer #(.width(16)) multiplexer_4 (
    .in0(bit_extender_4_out), .in1(bit_extender_3_out), .out(multiplexer_4_out), .sel(UII));  // open: en
  assign bit_extender_3_out = {{8{rom_1_data[8]}}, rom_1_data[8:1]};  // Bit_Extender bit_extender_3
  ALU alu_1 (
    .ReadDataT(multiplexer_3_out), .ReadDataS(registerfile_1_readdatas), .Oper(Oper), .Zero(Zero),
    .ALUout(alu_1_aluout), .Larger(L), .Smaller(S), .Upper(alu_1_upper), .Rem(alu_1_rem));
  assign bit_extender_4_out = {{8{1'b0}}, rom_1_data[8:1]};  // Bit_Extender bit_extender_4
  assign and_2_out = 16'hff & multiplexer_3_out;  // AND_Gate and_2, 16 bits wide
  Multiplexer #(.width(16)) multiplexer_5 (
    .in0(alu_1_aluout), .in1(registerfile_1_readdatas), .out(multiplexer_5_out), .sel(ARS));  // open: en
  Multiplexer #(.select(2), .width(8)) multiplexer_6 (
    .in0(adder_1_out), .in1(rom_1_data[8:1]), .in2(registerfile_1_readdatas[7:0]), .out(multiplexer_6_out),
    .sel(PCMux));  // open: in3, en
  RAM #(.dataWidth(16), .bus("separate")) ram_1 (
    .addr(and_2_out[7:0]), .din(multiplexer_5_out), .data(ram_1_data), .str(Str), .sel(DataMemory),
    .clk(clock_1_out), .ld(Ld));  // open: clr

  // Notes on the sheet:
  //   Name: Fransisca K. Larasati
  //   E-mail: FKL1@pitt.edu
  //   contents of rom_1 (hex, n*v repeats v):
  //   8200 b200 1202 2481 2440 15e0 6403 b001
endmodule
